// Logisim project carry-lookahead-adder.circ as structural Verilog: 2 circuits, main circuit main
module main (
  input  A0,
  input  A1,
  input  A2,
  input  A3,
  input  CarryIn,
  input  B0,
  input  B1,
  input  B2,
  input  B3,
  output S0,
  output S1,
  output S2,
  output S3,
  output CarryOut
);

  wire carry_lookahead_adder_1_c;

  carry_lookahead_adder carry_lookahead_adder_1 (
    .C0(CarryIn), .A0(A0), .B0(B0), .A1(A1), .B1(B1), .Q0(S0), .Q1(S1), .C(carry_lookahead_adder_1_c));
  carry_lookahead_adder carry_lookahead_adder_2 (
    .C0(carry_lookahead_adder_1_c), .A0(A2), .B0(B2), .A1(A3), .B1(B3), .Q0(S2), .Q1(S3), .C(CarryOut));
endmodule

module carry_lookahead_adder (
  input  C0,
  input  A0,
  input  B0,
  input  A1,
  input  B1,
  output Q0,
  output Q1,
  output C
);

  wire and_1_out, and_2_out, and_3_out, and_4_out, or_1_out, xor_1_out, xor_2_out;

  xor xor_1 (xor_1_out, A0, B0);
  and and_1 (and_1_out, A0, B0);
  xor xor_2 (xor_2_out, A1, B1);
  and and_2 (and_2_out, A1, B1);
  and and_3 (and_3_out, C0, xor_1_out);
  xor xor_3 (Q1, or_1_out, xor_2_out);
  xor xor_4 (Q0, C0, xor_1_out);
  or or_1 (or_1_out, and_3_out, and_1_out);
  and and_4 (and_4_out, or_1_out, xor_2_out);
  or or_2 (C, and_4_out, and_2_out);
endmodule
