// Logisim project carry-lookahead-adder.circ as structural Verilog: 4 circuits, main circuit main
module main (
  input  A0,
  input  A1,
  input  A2,
  input  A3,
  input  CarryIn,
  input  B0,
  input  B1,
  input  B2,
  input  B3,
  output S0,
  output S1,
  output S2,
  output S3,
  output CarryOut,
  output PG,
  output GG
);

  wire Carry__Look_Ahead_c1, Carry__Look_Ahead_c2, Carry__Look_Ahead_c3, full_adder_1_g, full_adder_1_p,
       full_adder_2_g, full_adder_2_p, full_adder_3_g, full_adder_3_p, full_adder_4_g, full_adder_4_p;

  full_adder full_adder_1 (.A(A0), .B(B0), .C_In(CarryIn), .S(S0), .P(full_adder_1_p), .G(full_adder_1_g));
  full_adder full_adder_2 (.A(A1), .B(B1), .C_In(Carry__Look_Ahead_c1), .S(S1), .P(full_adder_2_p), .G(full_adder_2_g));
  full_adder full_adder_3 (.A(A2), .B(B2), .C_In(Carry__Look_Ahead_c2), .S(S2), .P(full_adder_3_p), .G(full_adder_3_g));
  full_adder full_adder_4 (.A(A3), .B(B3), .C_In(Carry__Look_Ahead_c3), .S(S3), .P(full_adder_4_p), .G(full_adder_4_g));
  _4bits_carry_lookahead Carry__Look_Ahead (
    .C0(CarryIn), .P0(full_adder_1_p), .G0(full_adder_1_g), .P1(full_adder_2_p), .G1(full_adder_2_g),
    .P2(full_adder_3_p), .G2(full_adder_3_g), .P3(full_adder_4_p), .G3(full_adder_4_g),
    .C1(Carry__Look_Ahead_c1), .C2(Carry__Look_Ahead_c2), .C3(Carry__Look_Ahead_c3), .C4(CarryOut), .PG(PG),
    .GG(GG));
endmodule

module _4bits_carry_lookahead_adder (
  input  A0,
  input  A1,
  input  A2,
  input  A3,
  input  CarryIn,
  input  B0,
  input  B1,
  input  B2,
  input  B3,
  output S0,
  output S1,
  output S2,
  output S3,
  output CarryOut,
  output PG,
  output GG
);

  wire Carry__Look_Ahead_c1, Carry__Look_Ahead_c2, Carry__Look_Ahead_c3, full_adder_1_g, full_adder_1_p,
       full_adder_2_g, full_adder_2_p, full_adder_3_g, full_adder_3_p, full_adder_4_g, full_adder_4_p;

  full_adder full_adder_1 (.A(A0), .B(B0), .C_In(CarryIn), .S(S0), .P(full_adder_1_p), .G(full_adder_1_g));
  full_adder full_adder_2 (.A(A1), .B(B1), .C_In(Carry__Look_Ahead_c1), .S(S1), .P(full_adder_2_p), .G(full_adder_2_g));
  full_adder full_adder_3 (.A(A2), .B(B2), .C_In(Carry__Look_Ahead_c2), .S(S2), .P(full_adder_3_p), .G(full_adder_3_g));
  full_adder full_adder_4 (.A(A3), .B(B3), .C_In(Carry__Look_Ahead_c3), .S(S3), .P(full_adder_4_p), .G(full_adder_4_g));
  _4bits_carry_lookahead Carry__Look_Ahead (
    .C0(CarryIn), .P0(full_adder_1_p), .G0(full_adder_1_g), .P1(full_adder_2_p), .G1(full_adder_2_g),
    .P2(full_adder_3_p), .G2(full_adder_3_g), .P3(full_adder_4_p), .G3(full_adder_4_g),
    .C1(Carry__Look_Ahead_c1), .C2(Carry__Look_Ahead_c2), .C3(Carry__Look_Ahead_c3), .C4(CarryOut), .PG(PG),
    .GG(GG));
endmodule

// +
module full_adder (
  input  A,
  input  B,
  input  C_In,
  output S,
  output P,
  output G
);

  xor xor_1 (P, A, B);
  xor xor_2 (S, P, C_In);
  and and_1 (G, A, B);
endmodule

module _4bits_carry_lookahead (
  input  C0,
  input  P0,
  input  G0,
  input  P1,
  input  G1,
  input  P2,
  input  G2,
  input  P3,
  input  G3,
  output C1,
  output C2,
  output C3,
  output C4,
  output PG,
  output GG
);

  wire and_1_out, and_2_out, and_3_out, and_4_out, and_5_out, and_6_out, and_7_out;

  and and_1 (and_1_out, G0, P1, P2, P3);
  and and_2 (and_2_out, G1, P2, P3);
  and and_3 (and_3_out, P3, G2);
  and and_4 (and_4_out, C0, P0);
  and and_5 (and_5_out, C1, P1);
  and and_6 (and_6_out, C2, P2);
  and and_7 (and_7_out, C3, P3);
  or or_1 (C4, and_7_out, G3);
  or or_2 (GG, and_1_out, and_2_out, and_3_out, G3);
  or or_3 (C1, and_4_out, G0);
  or or_4 (C2, and_5_out, G1);
  or or_5 (C3, and_6_out, G2);
  and and_8 (PG, P0, P1, P2, P3);
endmodule
