// Logisim project cpu harvard.circ as structural Verilog: 10 circuits, main circuit ring counter
module ring_counter (
  input  Clock,
  input  Reset,
  output fetch,
  output decode,
  output execute
);

  wire and_1_out, d_ff_1_qn, d_ff_2_qn, d_ff_3_qn, or_1_out;

  or or_1 (or_1_out, and_1_out, execute);
  D_Flip_Flop d_ff_1 (.clk(Clock), .D(or_1_out), .Q(fetch), .Qn(d_ff_1_qn), .reset(Reset));  // open: preset, en
  and and_1 (and_1_out, d_ff_2_qn, d_ff_1_qn, d_ff_3_qn);
  D_Flip_Flop d_ff_2 (.clk(Clock), .D(fetch), .Q(decode), .Qn(d_ff_2_qn), .reset(Reset));  // open: preset, en
  D_Flip_Flop d_ff_3 (.clk(Clock), .D(decode), .Q(execute), .Qn(d_ff_3_qn), .reset(Reset));  // open: preset, en
endmodule

module main (
  input  Reset,
  output [7:0] out_2,
  output out_3,
  output out_4,
  output out_5,
  output out_6,
  output out_7,
  output [2:0] out_8
);

  wire ALU_carry_out, ALU_cs_cmp, ALU_equal, ALU_inf, ALU_sup, clock_1_out, Contol_Jump_Unit_inc_jump,
       Contol_Jump_Unit_jump_immed, decoder_1_add_reg, decoder_1_and_reg, decoder_1_cmp,
       decoder_1_jump_immed, decoder_1_jumpeq, decoder_1_load_reg__addr, decoder_1_mov_acc1__reg,
       decoder_1_mov_acc2__reg, decoder_1_mov_reg__immed, decoder_1_mov_reg__reg, decoder_1_or_reg,
       decoder_1_reset, decoder_1_store_addr__reg, decoder_1_xor_reg, micro_instr_matrix_1_cs1,
       micro_instr_matrix_1_cs2, micro_instr_matrix_1_cs3, micro_instr_matrix_1_cs4,
       micro_instr_matrix_1_cs5, micro_instr_matrix_1_cs6, micro_instr_matrix_1_cs7,
       micro_instr_matrix_1_cs8, micro_instr_matrix_1_cs9, micro_instr_matrix_1_cs11_reset, not_1_out,
       or_1_out, RING_COUNTER_decode, RING_COUNTER_execute, RING_COUNTER_fetch;
  wire [1:0] instruction_splitter_1_dst, instruction_splitter_1_src, micro_instr_matrix_1_cs12;
  wire [3:0] instruction_splitter_1_opcode;
  wire [7:0] controlled_buffer_1_out, PC_q;
  wire [15:0] IR_q, rom_1_data;

  ring_counter RING_COUNTER (
    .Clock(clock_1_out), .Reset(Reset), .fetch(RING_COUNTER_fetch), .decode(RING_COUNTER_decode),
    .execute(RING_COUNTER_execute));
  assign controlled_buffer_1_out = micro_instr_matrix_1_cs9 ? out_2 : 8'bz;  // Controlled_Buffer controlled_buffer_1
  Clock clock_1 (.out(clock_1_out));
  Jump_Control_Unit Contol_Jump_Unit (
    .CS_Jump(micro_instr_matrix_1_cs6), .CS_Jump_Type(micro_instr_matrix_1_cs12), .Equal(out_6),
    .Jump_Immed(Contol_Jump_Unit_jump_immed), .Inc_Jump(Contol_Jump_Unit_inc_jump));  // open: Inf, Sup
  RAM #(.bus("asynch")) ram_1 (
    .addr(out_2), .data(controlled_buffer_1_out), .sel(micro_instr_matrix_1_cs7),
    .ld(micro_instr_matrix_1_cs8));  // open: clr
  ROM #(.dataWidth(16)) rom_1 (.addr(PC_q), .data(rom_1_data));  // open: sel
  Counter PC (
    .load(Contol_Jump_Unit_jump_immed), .D(controlled_buffer_1_out), .count(Contol_Jump_Unit_inc_jump),
    .Q(PC_q), .clk(RING_COUNTER_execute), .clr(Reset));  // open: carry
  Registers REGISTERS (
    .IN(controlled_buffer_1_out), .Clock(RING_COUNTER_execute), .Select_IN(instruction_splitter_1_dst),
    .Enable__Write(micro_instr_matrix_1_cs1), .Reset(Reset), .Select_OUT(instruction_splitter_1_src),
    .CS_OUT(micro_instr_matrix_1_cs2), .OUT(controlled_buffer_1_out));
  Register #(.width(16)) IR (.D(rom_1_data), .Q(IR_q), .clk(RING_COUNTER_fetch), .clr(Reset));  // open: en
  instruction_splitter instruction_splitter_1 (
    .INSTR(IR_q), .CONSTANTE(out_2), .SRC(instruction_splitter_1_src), .DST(instruction_splitter_1_dst),
    .OPCODE(instruction_splitter_1_opcode));
  or or_1 (or_1_out, RING_COUNTER_decode, RING_COUNTER_execute);
  decoder decoder_1 (
    .opcode(instruction_splitter_1_opcode), .Enable(or_1_out), .RESET(decoder_1_reset),
    .mov_reg__reg(decoder_1_mov_reg__reg), .mov_reg__immed(decoder_1_mov_reg__immed),
    .mov_acc1__reg(decoder_1_mov_acc1__reg), .mov_acc2__reg(decoder_1_mov_acc2__reg),
    .add_reg(decoder_1_add_reg), .xor_reg(decoder_1_xor_reg), .or_reg(decoder_1_or_reg),
    .and_reg(decoder_1_and_reg), .jump_immed(decoder_1_jump_immed),
    .store_addr__reg(decoder_1_store_addr__reg), .load_reg__addr(decoder_1_load_reg__addr),
    .Cmp(decoder_1_cmp), .Jumpeq(decoder_1_jumpeq));
  not not_1 (not_1_out, ALU_cs_cmp);
  ALU ALU (
    .ACC1(controlled_buffer_1_out), .CS_ACC1(micro_instr_matrix_1_cs3), .Clock(RING_COUNTER_execute),
    .CS_ACC2(micro_instr_matrix_1_cs4), .ACC2(controlled_buffer_1_out), .Reset(Reset), .CARRY_IN(out_4),
    .CARRY_OUT(ALU_carry_out), .sup(ALU_sup), .equal(ALU_equal), .inf(ALU_inf), .CS_Cmp(ALU_cs_cmp),
    .Select_ALU(out_8), .CS_ALU(micro_instr_matrix_1_cs5), .OUTi(controlled_buffer_1_out));
  micro_instr_matrix micro_instr_matrix_1 (
    ._0(decoder_1_reset), ._1(decoder_1_mov_reg__reg), ._2(decoder_1_mov_reg__immed),
    ._3(decoder_1_mov_acc1__reg), ._4(decoder_1_mov_acc2__reg), ._5(decoder_1_add_reg),
    ._6(decoder_1_xor_reg), ._7(decoder_1_or_reg), ._8(decoder_1_and_reg), ._9(decoder_1_jump_immed),
    ._10(decoder_1_store_addr__reg), ._11(decoder_1_load_reg__addr), ._12(decoder_1_cmp),
    ._13(decoder_1_jumpeq), .CS1(micro_instr_matrix_1_cs1), .CS2(micro_instr_matrix_1_cs2),
    .CS3(micro_instr_matrix_1_cs3), .CS4(micro_instr_matrix_1_cs4), .CS5(micro_instr_matrix_1_cs5),
    .CS6(micro_instr_matrix_1_cs6), .CS7(micro_instr_matrix_1_cs7), .CS8(micro_instr_matrix_1_cs8),
    .CS9(micro_instr_matrix_1_cs9), .CS10(out_8), .CS11_Reset(micro_instr_matrix_1_cs11_reset),
    .CS12(micro_instr_matrix_1_cs12));
  registers_flags registers_flags_1 (
    .DATA(controlled_buffer_1_out), .CARRY(ALU_carry_out), .SUP(ALU_sup), .EQUAL(ALU_equal), .INF(ALU_inf),
    .CS_CMP(ALU_cs_cmp), .CS_Z_C(not_1_out), .Clock(RING_COUNTER_execute), .RESET(Reset), .ZERO(out_3),
    .CARRY_FLAG(out_4), .SUP_2(out_5), .EQUAL_2(out_6), .INF_2(out_7));

  // Notes on the sheet:
  //   contents of rom_1 (hex, n*v repeats v):
  //   240a 2800 2c01 3300 4200 5800 a200 3200 4100 c000 d00a 9003
endmodule

module ALU (
  input  CARRY_IN,
  input  [7:0] ACC1,
  input  CS_ACC1,
  input  Clock,
  input  CS_ACC2,
  input  [7:0] ACC2,
  input  [2:0] Select_ALU,
  input  CS_ALU,
  input  Reset,
  output sup,
  output equal,
  output inf,
  output CS_Cmp,
  output CARRY_OUT,
  output [7:0] OUTi
);

  wire [7:0] adder_1_out, and_1_out, or_1_out, register_1_q, register_2_q, xor_1_out;

  Register register_1 (.D(ACC1), .en(CS_ACC1), .Q(register_1_q), .clk(Clock), .clr(Reset));
  Register register_2 (.D(ACC2), .en(CS_ACC2), .Q(register_2_q), .clk(Clock), .clr(Reset));
  Adder adder_1 (.a(register_1_q), .b(register_2_q), .out(adder_1_out), .cin(CARRY_IN), .cout(CARRY_OUT));
  assign xor_1_out = register_1_q ^ register_2_q;  // XOR_Gate xor_1, 8 bits wide
  assign or_1_out = register_1_q | register_2_q;  // OR_Gate or_1, 8 bits wide
  assign and_1_out = register_1_q & register_2_q;  // AND_Gate and_1, 8 bits wide
  Comparator #(.mode("unsigned")) comparator_1 (.a(register_1_q), .b(register_2_q), .gt(sup), .eq(equal), .lt(inf));
  Multiplexer #(.select(3), .width(8)) multiplexer_1 (
    .in0(adder_1_out), .in1(xor_1_out), .in2(or_1_out), .in3(and_1_out), .out(OUTi), .sel(Select_ALU),
    .en(CS_ALU));  // open: in4, in5, in6, in7

  assign CS_Cmp = Select_ALU[2];
endmodule

module Registers (
  input  [7:0] IN,
  input  Clock,
  input  CS_OUT,
  input  [1:0] Select_OUT,
  input  [1:0] Select_IN,
  input  Enable__Write,
  input  Reset,
  output [7:0] OUT
);

  wire demultiplexer_1_out0, demultiplexer_1_out1, demultiplexer_1_out2, demultiplexer_1_out3;
  wire [7:0] register_1_q, register_2_q, register_3_q, register_4_q;

  Demultiplexer #(.select(2)) demultiplexer_1 (
    .out0(demultiplexer_1_out0), .out1(demultiplexer_1_out1), .out2(demultiplexer_1_out2),
    .out3(demultiplexer_1_out3), .in(Enable__Write), .sel(Select_IN));  // open: en
  Register register_1 (.D(IN), .en(demultiplexer_1_out0), .Q(register_1_q), .clk(Clock), .clr(Reset));
  Register register_2 (.D(IN), .en(demultiplexer_1_out1), .Q(register_2_q), .clk(Clock), .clr(Reset));
  Register register_3 (.D(IN), .en(demultiplexer_1_out2), .Q(register_3_q), .clk(Clock), .clr(Reset));
  Register register_4 (.D(IN), .en(demultiplexer_1_out3), .Q(register_4_q), .clk(Clock), .clr(Reset));
  Multiplexer #(.select(2), .width(8)) multiplexer_1 (
    .in0(register_1_q), .in1(register_2_q), .in2(register_3_q), .in3(register_4_q), .out(OUT),
    .sel(Select_OUT), .en(CS_OUT));
endmodule

// DECODER
module decoder (
  input  [3:0] opcode,
  input  Enable,
  output RESET,
  output mov_reg__reg,
  output mov_reg__immed,
  output mov_acc1__reg,
  output mov_acc2__reg,
  output add_reg,
  output xor_reg,
  output or_reg,
  output and_reg,
  output jump_immed,
  output store_addr__reg,
  output load_reg__addr,
  output Cmp,
  output Jumpeq
);

  wire and_1_out, and_2_out, and_3_out, and_4_out, and_5_out, and_6_out, and_7_out, and_8_out, and_9_out,
       and_10_out, and_11_out, and_12_out, and_13_out, and_14_out, not_1_out, not_2_out, not_3_out, not_4_out;

  not not_1 (not_1_out, opcode[0]);
  not not_2 (not_2_out, opcode[1]);
  not not_3 (not_3_out, opcode[2]);
  not not_4 (not_4_out, opcode[3]);
  and and_1 (and_1_out, not_1_out, not_2_out, not_3_out, not_4_out);
  and and_2 (and_2_out, opcode[0], not_2_out, not_3_out, not_4_out);
  and and_3 (and_3_out, not_1_out, opcode[1], not_3_out, not_4_out);
  and and_4 (and_4_out, opcode[0], opcode[1], not_3_out, not_4_out);
  and and_5 (and_5_out, not_1_out, not_2_out, opcode[2], not_4_out);
  and and_6 (and_6_out, opcode[0], not_2_out, opcode[2], not_4_out);
  and and_7 (and_7_out, not_1_out, opcode[1], opcode[2], not_4_out);
  and and_8 (and_8_out, opcode[0], opcode[1], opcode[2], not_4_out);
  and and_9 (and_9_out, not_1_out, not_2_out, not_3_out, opcode[3]);
  and and_10 (and_10_out, opcode[0], not_2_out, not_3_out, opcode[3]);
  and and_11 (and_11_out, not_1_out, opcode[1], not_3_out, opcode[3]);
  and and_12 (and_12_out, opcode[0], opcode[1], not_3_out, opcode[3]);
  and and_13 (and_13_out, opcode[3], opcode[2], not_2_out, not_1_out);
  and and_14 (and_14_out, opcode[3], opcode[2], not_2_out, opcode[0]);
  and and_15 (RESET, and_1_out, Enable);
  and and_16 (mov_reg__reg, and_2_out, Enable);
  and and_17 (mov_reg__immed, and_3_out, Enable);
  and and_18 (mov_acc1__reg, and_4_out, Enable);
  and and_19 (mov_acc2__reg, and_5_out, Enable);
  and and_20 (add_reg, and_6_out, Enable);
  and and_21 (xor_reg, and_7_out, Enable);
  and and_22 (or_reg, and_8_out, Enable);
  and and_23 (and_reg, and_9_out, Enable);
  and and_24 (jump_immed, and_10_out, Enable);
  and and_25 (store_addr__reg, and_11_out, Enable);
  and and_26 (load_reg__addr, and_12_out, Enable);
  and and_27 (Cmp, and_13_out, Enable);
  and and_28 (Jumpeq, Enable, and_14_out);
endmodule

// M. INSTR MATRIX
module micro_instr_matrix (
  input  _0,
  input  _1,
  input  _2,
  input  _3,
  input  _4,
  input  _5,
  input  _6,
  input  _7,
  input  _8,
  input  _9,
  input  _10,
  input  _11,
  input  _12,
  input  _13,
  output CS1,
  output CS2,
  output CS3,
  output CS4,
  output CS5,
  output CS6,
  output CS7,
  output CS8,
  output CS9,
  output [2:0] CS10,
  output CS11_Reset,
  output [1:0] CS12
);

  wire or_1_out, or_2_out;

  buf or_1 (or_1_out, _13);  // OR_Gate
  or or_2 (or_2_out, _1, _2, _11, _7, _8);
  or or_3 (CS2, _1, _3, _4, _10);
  buf or_4 (CS3, _3);  // OR_Gate
  buf or_5 (CS4, _4);  // OR_Gate
  or or_6 (CS5, _7, _8, _6, _5);
  or or_7 (CS6, _9, _13);
  or or_8 (CS7, _11, _10);
  buf or_9 (CS8, _11);  // OR_Gate
  or or_10 (CS9, _2, _9, _13);
  or or_11 (CS10[0], _8, _6);
  or or_12 (CS10[1], _7, _8);
  or or_13 (CS1, or_2_out, _6, _5);
  assign CS12 = {{1{1'b0}}, or_1_out};  // Bit_Extender bit_extender_1

  assign CS10[2] = _12;
  assign CS11_Reset = _0;
endmodule

module instruction_splitter (
  input  [15:0] INSTR,
  output [7:0] CONSTANTE,
  output [1:0] SRC,
  output [1:0] DST,
  output [3:0] OPCODE
);


  assign CONSTANTE = INSTR[7:0];
  assign DST = INSTR[11:10];
  assign OPCODE = INSTR[15:12];
  assign SRC = INSTR[9:8];
endmodule

module zero_door (
  input  [7:0] INPUT,
  output OUTPUT
);

  wire or_1_out;

  not not_1 (OUTPUT, or_1_out);
  or or_1 (or_1_out, INPUT[0], INPUT[1], INPUT[2], INPUT[3], INPUT[4], INPUT[5], INPUT[6], INPUT[7]);
endmodule

module registers_flags (
  input  CS_CMP,
  input  CS_Z_C,
  input  Clock,
  input  [7:0] DATA,
  input  CARRY,
  input  SUP,
  input  EQUAL,
  input  INF,
  input  RESET,
  output ZERO,
  output CARRY_FLAG,
  output SUP_2,
  output EQUAL_2,
  output INF_2
);

  wire zero_door_1_output;

  zero_door zero_door_1 (.INPUT(DATA), .OUTPUT(zero_door_1_output));
  Register #(.width(1)) register_1 (.D(zero_door_1_output), .en(CS_Z_C), .Q(ZERO), .clk(Clock), .clr(RESET));
  Register #(.width(1)) register_2 (.D(CARRY), .en(CS_Z_C), .Q(CARRY_FLAG), .clk(Clock), .clr(RESET));
  Register #(.width(1)) register_3 (.D(SUP), .en(CS_CMP), .Q(SUP_2), .clk(Clock), .clr(RESET));
  Register #(.width(1)) register_4 (.D(EQUAL), .en(CS_CMP), .Q(EQUAL_2), .clk(Clock), .clr(RESET));
  Register #(.width(1)) register_5 (.D(INF), .en(CS_CMP), .Q(INF_2), .clk(Clock), .clr(RESET));
endmodule

module Jump_Control_Unit (
  input  CS_Jump,
  input  [1:0] CS_Jump_Type,
  input  Equal,
  input  Inf,
  input  Sup,
  output Jump_Immed,
  output Inc_Jump
);

  wire and_1_out, and_2_out, not_1_out, not_2_out;

  not not_1 (not_1_out, CS_Jump_Type[0]);
  not not_2 (not_2_out, CS_Jump_Type[1]);
  and and_1 (and_1_out, Equal, CS_Jump_Type[0], not_2_out, CS_Jump);
  and and_2 (and_2_out, CS_Jump, not_1_out, not_2_out);
  or or_1 (Jump_Immed, and_2_out, and_1_out);
  not not_3 (Inc_Jump, Jump_Immed);
endmodule
